# Fritzing sketch weatherman (saved by Fritzing 0.9.3b)
perfboards: 2

parts:
  R1 = Resistor [tolerance=±5% resistance=10k package=THT]
  C1 = Ceramic Capacitor [capacitance=100nF package="100 mil [THT, multilayer]"]
  Power_plug1 = Power plug
  LED1 = LED - 5mm [color="Red (633nm)" package="5 mm [THT]"]
  R2 = Resistor [tolerance=±5% resistance=100 package=THT]
  J7 = shrouded pin header, 12 pins [form="♂ (shrouded male)"]
  C2 = Ceramic Capacitor [capacitance=100nF package="100 mil [THT, multilayer]"]
  U1 = RJ45 Jack [package=rj45-8]
  J1 = male pin header, 9 pins [form="♂ (male)"]
  J8 = male pin header, 9 pins [form="♂ (male)"]  # not connected
  J5 = male pin header, 9 pins [form="♂ (male)"]
  J4 = male pin header, 9 pins [form="♂ (male)"]
  R3 = Resistor [tolerance=±5% resistance=10k package=THT]
  J9 = male pin header, 2 pins [form="♂ (male)"]
  J10 = male pin header, 2 pins [form="♂ (male)"]
  U2 = RJ45 Jack [package=rj45-8]
  JP2 = Header 4 [package=molex-1x4_lock]
  JP3 = Header 4 [package=molex-1x4_lock]
  JP4 = Header 4 [package=molex-1x4_lock]
  R4 = Resistor [tolerance=±5% resistance=100 package=THT]
  LED2 = LED - 5mm [color="Red (633nm)" package="5 mm [THT]"]
  J11 = RJ11 Jack [package=rj11-6]
  J12 = RJ11 Jack [package=rj11-6]

nets:
  N1: R1.Pin_0, C1.1, J7.pin12, J4.pin8
  N2: R1.Pin_1, C2.1, U1.2, J5.pin9, J10.pin1
  N3: C1.0, LED1.cathode, J7.pin6, C2.0, J4.pin9, R3.Pin_1, J10.pin2
  N4: Power_plug1.GND, J9.pin2
  N5: Power_plug1.VCC, J9.pin1
  N6: LED1.anode, R2.Pin_1
  N7: R2.Pin_0, U1.5, J4.pin4
  N8: J7.pin1, J4.pin2
  N9: J7.pin4, J5.pin7
  N10: J7.pin5, J5.pin8
  N11: U1.3, J5.pin6
  N12: U1.4, J4.pin6
  N13: U1.6, J1.pin4
  N14: U1.7, J1.pin8, R3.Pin_0
  N15: U1.8, J1.pin7
  N16: U2.1, JP2.2, JP3.2, JP4.2, LED2.cathode, J11.3, J12.3
  N17: U2.2, JP2.1, JP3.1, JP4.1, J11.2
  N18: U2.3, JP2.4, JP3.4, JP4.4
  N19: U2.4, JP2.3, JP3.3, JP4.3
  N20: U2.5, R4.Pin_0
  N21: U2.6, J12.4
  N22: U2.7, J11.5
  N23: U2.8, J11.4
  N24: R4.Pin_1, LED2.anode
